// Logisim project CircuitoIntegrado.circ as structural Verilog: 1 circuit, main circuit main
module main (
  input  [15:0] Instruction_In,
  output [2:0] out_2,
  output [3:0] \Cálculo_do_jump ,
  output [3:0] Debug_RA,
  output [3:0] out_5,
  output [3:0] out_6,
  output [3:0] Debug_ULA,
  output [3:0] Debug_PC,
  output [15:0] Debug_IM,
  output [3:0] out_10,
  output [15:0] \Debug_Escrita_na_memória 
);

  wire comparator_1_eq, M_decoder_clock_r0_output, M_decoder_clock_r1_output, Uc_p1, Uc_p2, Uc_p3, undriven,
       undriven_2, undriven_3, undriven_4, undriven_5;
  wire [3:0] M_decoder_output_r0, M_decoder_output_r1, multiplexer_1_out;
  wire [15:0] IR_out_3, multiplexer_2_out;

  Register RA (.Data_In(Instruction_In[3:0]), .Clock(undriven_5), .Data_Out(Debug_RA));
  Register PC (.Data_In(\Cálculo_do_jump ), .Clock(Uc_p1), .Data_Out(Debug_PC));
  Multiplexer #(.width(4), .enable("false")) multiplexer_1 (
    .in0(Debug_RA), .in1(Debug_PC), .out(multiplexer_1_out), .sel(Uc_p2));
  SelectDataMemory_main main_1 (
    .Estado(3'b110), .R0(out_6), .R1(out_10), .Instruction(Instruction_In), .out_5(\Debug_Escrita_na_memória ));
  IR_main IR (.in_2(Debug_IM), .in_1(Uc_p3), .out_3(IR_out_3));
  Instruction_Memory IM (
    .Data_to_Save(\Debug_Escrita_na_memória ), .Data_to_Read(Debug_IM), .Adress_to_Write(multiplexer_1_out),
    .Write_State(undriven_2), .Adress_to_Read(multiplexer_1_out));
  Multiplexer #(.width(16), .enable("false")) multiplexer_2 (
    .in0(IR_out_3), .in1({16{1'b0}}), .out(multiplexer_2_out), .sel(undriven));
  // Send_Signal Uc: pin names not known; wires that end beside it: Uc_p1, Uc_p2, Uc_p3, out_2
  Comparator #(.width(3)) comparator_1 (.a(3'b110), .b(3'b111), .eq(comparator_1_eq));  // open: gt, lt
  Register R0 (.Data_In(M_decoder_output_r0), .Clock(M_decoder_clock_r0_output), .Data_Out(out_6));
  MoveDecoder_main M_decoder (
    .Estado(3'b110), .Operandos(multiplexer_2_out[11:8]), .Clock_R1(undriven_3), .Clock_R0(undriven_4),
    .R0_data(multiplexer_2_out[11:8]), .RA(multiplexer_2_out[3:0]), .R1_data(multiplexer_2_out[7:4]),
    .Clock_R1_Output(M_decoder_clock_r1_output), .Clock_R0_Output(M_decoder_clock_r0_output),
    .Output_R0(M_decoder_output_r0), .Output_R1(M_decoder_output_r1));
  Register R1 (.Data_In(M_decoder_output_r1), .Clock(M_decoder_clock_r1_output), .Data_Out(out_10));
  JumpDecoder_main main_2 (
    .Gambiarra_do_estado(3'b110), .PC(Debug_PC), .RA(Debug_RA), .Is_Jump_Instruction(comparator_1_eq),
    .out_5(\Cálculo_do_jump ));
  ULA ula_1 (.Entry_A(out_6), .Entry_B(out_10), .Out(Debug_ULA), .OPCODE(out_5));  // open: Carry__iN, Carry_Out
endmodule
