// Logisim project IR.circ as structural Verilog: 2 circuits, main circuit main
module main (
  input  in_1,
  input  [15:0] in_2,
  output [15:0] out_3
);

  Register register_1 (.Data_In(in_2[3:0]), .Clock(in_1), .Data_Out(out_3[3:0]));
  Register register_2 (.Data_In(in_2[7:4]), .Clock(in_1), .Data_Out(out_3[7:4]));
  Register register_3 (.Data_In(in_2[11:8]), .Clock(in_1), .Data_Out(out_3[11:8]));
  Register register_4 (.Data_In(in_2[15:12]), .Clock(in_1), .Data_Out(out_3[15:12]));
endmodule

module Register (
  input  [3:0] Data_In,
  input  Clock,
  output [3:0] Data_Out
);

  D_Flip_Flop d_ff_1 (.clk(Clock), .D(Data_In[0]), .Q(Data_Out[0]));  // open: Qn, preset, en, reset
  D_Flip_Flop d_ff_2 (.clk(Clock), .D(Data_In[1]), .Q(Data_Out[1]));  // open: Qn, preset, en, reset
  D_Flip_Flop d_ff_3 (.clk(Clock), .D(Data_In[2]), .Q(Data_Out[2]));  // open: Qn, preset, en, reset
  D_Flip_Flop d_ff_4 (.clk(Clock), .D(Data_In[3]), .Q(Data_Out[3]));  // open: Qn, preset, en, reset
endmodule
