// Logisim project JumpDecoder.circ as structural Verilog: 1 circuit, main circuit main
module main (
  input  Is_Jump_Instruction,
  input  [3:0] PC,
  input  [3:0] RA,
  output [3:0] out_4
);

  wire comparator_1_eq;
  wire [3:0] adder_1_out, adder_2_out, multiplexer_1_out;

  Adder #(.width(4)) adder_1 (.a(PC), .b(4'b0001), .out(adder_1_out));  // open: cin, cout
  Adder #(.width(4)) adder_2 (.a(PC), .b(RA), .out(adder_2_out));  // open: cin, cout
  Multiplexer #(.width(4), .enable("false")) multiplexer_1 (
    .in0(adder_1_out), .in1(adder_2_out), .out(multiplexer_1_out), .sel(Is_Jump_Instruction));
  Comparator #(.width(4)) comparator_1 (.a(PC), .b(4'b1111), .eq(comparator_1_eq));  // open: gt, lt
  Multiplexer #(.width(4), .enable("false")) multiplexer_2 (
    .in0(multiplexer_1_out), .in1(4'b0000), .out(out_4), .sel(comparator_1_eq));

  // Notes on the sheet:
  //   <!--Gambiarra enxuta!!!-->
endmodule
