// Logisim project ULA.circ as structural Verilog: 1 circuit, main circuit ULA
module ULA (
  input  Carry__iN,
  input  [3:0] OPCODE,
  input  [3:0] Entry_A,
  input  [3:0] Entry_B,
  output [3:0] Out,
  output Carry_Out
);

  wire [3:0] adder_1_out, and_1_out, nand_1_out, nor_1_out, or_1_out, subtractor_1_out, xnor_1_out, xor_1_out;

  Adder #(.width(4)) adder_1 (.a(Entry_A), .b(Entry_B), .out(adder_1_out), .cin(Carry__iN), .cout(Carry_Out));
  Subtractor #(.width(4)) subtractor_1 (
    .a(Entry_A), .b(Entry_B), .out(subtractor_1_out), .bin(Carry__iN), .bout(Carry_Out));
  assign or_1_out = Entry_A | Entry_B;  // OR_Gate or_1, 4 bits wide
  assign and_1_out = Entry_A & Entry_B;  // AND_Gate and_1, 4 bits wide
  assign xor_1_out = Entry_A ^ Entry_B;  // XOR_Gate xor_1, 4 bits wide
  assign nand_1_out = ~(Entry_A & Entry_B);  // NAND_Gate nand_1, 4 bits wide
  assign nor_1_out = ~(Entry_A | Entry_B);  // NOR_Gate nor_1, 4 bits wide
  assign xnor_1_out = ~(Entry_A ^ Entry_B);  // XNOR_Gate xnor_1, 4 bits wide
  Multiplexer #(.select(4), .width(4)) multiplexer_1 (
    .in0(Entry_B), .in1(adder_1_out), .in2(subtractor_1_out), .in3(or_1_out), .in4(and_1_out),
    .in5(xor_1_out), .in6(nand_1_out), .in7(nor_1_out), .in8(xnor_1_out), .out(Out), .sel(OPCODE));  // open: in9, in10, in11, in12, in13, in14, in15, en
endmodule
