// Logisim project Uc.circ as structural Verilog: 5 circuits, main circuit sequencer
module sequencer (
  input  [2:0] estado_atual,
  input  [3:0] opcode,
  input  [3:0] Registers,
  output [2:0] out_4
);

  wire A_Type_is_type_a, and_1_out, and_2_out, and_3_out, and_4_out, and_5_out, and_6_out, and_7_out,
       comparator_1_eq, comparator_2_eq, comparator_3_eq, comparator_4_eq, comparator_5_eq, comparator_5_gt,
       comparator_5_lt, J_Type_is_type_j, M_Type_is_m_type, or_1_out;

  AType A_Type (.Opcode(opcode), .Is_Type_A(A_Type_is_type_a));
  Comparator #(.width(4), .mode("unsigned")) comparator_1 (
    .a(opcode), .b(4'b1100), .eq(comparator_1_eq));  // open: gt, lt
  JType J_Type (.Opcode(opcode), .Is_Type_J(J_Type_is_type_j));
  MType M_Type (.in_1(opcode), .Is_M_Type(M_Type_is_m_type));
  Comparator #(.width(3), .mode("unsigned")) comparator_2 (
    .a(estado_atual), .b(3'b000), .eq(comparator_2_eq));  // open: gt, lt
  Comparator #(.width(3), .mode("unsigned")) comparator_3 (
    .a(estado_atual), .b(3'b010), .eq(comparator_3_eq));  // open: gt, lt
  Comparator #(.width(3), .mode("unsigned")) comparator_4 (
    .a(estado_atual), .b(3'b001), .eq(comparator_4_eq));  // open: gt, lt
  and and_1 (and_1_out, 1'b1, comparator_4_eq);
  and and_2 (and_2_out, comparator_3_eq, A_Type_is_type_a);
  and and_3 (and_3_out, comparator_3_eq, comparator_1_eq);
  and and_4 (and_4_out, comparator_3_eq, J_Type_is_type_j);
  and and_5 (and_5_out, comparator_3_eq, M_Type_is_m_type);
  Comparator #(.width(2)) comparator_5 (
    .a(Registers[3:2]), .b(2'b11), .gt(comparator_5_gt), .eq(comparator_5_eq), .lt(comparator_5_lt));
  or or_1 (or_1_out, comparator_5_gt, comparator_5_lt);
  and and_6 (and_6_out, and_5_out, comparator_5_eq);
  and and_7 (and_7_out, and_5_out, or_1_out);
  or or_2 (out_4[0], comparator_2_eq, and_2_out, and_4_out, and_7_out);
  or or_3 (out_4[1], and_1_out, and_2_out, and_4_out, and_6_out);
  or or_4 (out_4[2], and_3_out, and_4_out, and_5_out);

  // Notes on the sheet:
  //   RS
  //   RD
  //   A-Type CMP
  //   Estados
  //   J-Type= estado 1,2, 7
  //   A-Type = estado 1,2, 3 ou 4
  //   M-Type= estado 1,2, 5 ou 6
endmodule

module AType (
  input  [3:0] Opcode,
  output Is_Type_A
);

  wire comparator_1_gt, comparator_2_lt;

  Comparator #(.width(4), .mode("unsigned")) comparator_1 (
    .a(Opcode), .b(4'b0000), .gt(comparator_1_gt));  // open: eq, lt
  Comparator #(.width(4), .mode("unsigned")) comparator_2 (
    .a(Opcode), .b(4'b1100), .lt(comparator_2_lt));  // open: gt, eq
  and and_1 (Is_Type_A, comparator_1_gt, comparator_2_lt);
endmodule

module JType (
  input  [3:0] Opcode,
  output Is_Type_J
);

  wire comparator_1_gt, comparator_2_eq, comparator_2_lt, or_1_out;

  Comparator #(.width(4), .mode("unsigned")) comparator_1 (
    .a(Opcode), .b(4'b1100), .gt(comparator_1_gt));  // open: eq, lt
  Comparator #(.width(4), .mode("unsigned")) comparator_2 (
    .a(Opcode), .b(4'b1111), .eq(comparator_2_eq), .lt(comparator_2_lt));  // open: gt
  or or_1 (or_1_out, comparator_2_eq, comparator_2_lt);
  and and_1 (Is_Type_J, comparator_1_gt, or_1_out);
endmodule

module Send_Signal (
  input  [2:0] in_1,
  input  [15:0] Decoded_Instruction,
  output [2:0] state,
  output Clock_IR,
  output Select_input_MUX_MEM,
  output Clock_PC,
  output Clock_RA,
  output Clock_R0,
  output Clock_R1,
  output [3:0] Select_ULA_operation,
  output Write_MEM,
  output Select_Input_MUX_ULA
);

  wire and_1_out, and_2_out, and_3_out, clock_1_out, clock_2_out, clock_3_out, clock_4_out, clock_5_out,
       comparator_2_eq, comparator_4_eq, comparator_5_eq, comparator_6_eq, comparator_7_eq, comparator_8_eq,
       comparator_9_eq, comparator_10_eq, or_2_out, or_5_out, or_6_out;
  wire [1:0] multiplexer_2_out, multiplexer_3_out;

  sequencer Sequencer (
    .estado_atual(in_1), .opcode(Decoded_Instruction[15:12]), .Registers(Decoded_Instruction[11:8]),
    .out_4(state));
  Comparator #(.width(3), .mode("unsigned")) comparator_1 (
    .a(in_1), .b(3'b001), .eq(Select_input_MUX_MEM));  // open: gt, lt
  Comparator #(.width(3), .mode("unsigned")) comparator_2 (.a(in_1), .b(3'b000), .eq(comparator_2_eq));  // open: gt, lt
  Clock clock_1 (.out(clock_1_out));
  Comparator #(.width(3), .mode("unsigned")) comparator_3 (.a(in_1), .b(3'b010), .eq(Clock_RA));  // open: gt, lt
  Comparator #(.width(3), .mode("unsigned")) comparator_4 (.a(in_1), .b(3'b111), .eq(comparator_4_eq));  // open: gt, lt
  Comparator #(.width(3), .mode("unsigned")) comparator_5 (.a(in_1), .b(3'b101), .eq(comparator_5_eq));  // open: gt, lt
  Comparator #(.width(3), .mode("unsigned")) comparator_6 (.a(in_1), .b(3'b011), .eq(comparator_6_eq));  // open: gt, lt
  Comparator #(.width(3), .mode("unsigned")) comparator_7 (.a(in_1), .b(3'b100), .eq(comparator_7_eq));  // open: gt, lt
  Comparator #(.width(3), .mode("unsigned")) comparator_8 (.a(in_1), .b(3'b110), .eq(comparator_8_eq));  // open: gt, lt
  and and_1 (and_1_out, comparator_2_eq, clock_1_out);
  Clock clock_2 (.out(clock_2_out));
  and and_2 (and_2_out, Clock_RA, clock_3_out);
  Clock clock_3 (.out(clock_3_out));
  or or_1 (Clock_PC, Select_input_MUX_MEM, and_1_out, comparator_4_eq);
  or or_2 (or_2_out, comparator_6_eq, comparator_7_eq);
  or or_3 (Write_MEM, comparator_8_eq, and_3_out);
  and and_3 (and_3_out, Clock_RA, clock_2_out);
  or or_4 (Clock_IR, Select_input_MUX_MEM, and_2_out);
  Multiplexer #(.width(4)) multiplexer_1 (
    .in0(4'b0000), .in1(Decoded_Instruction[15:12]), .out(Select_ULA_operation), .sel(or_2_out));  // open: en
  Multiplexer #(.width(2)) multiplexer_2 (
    .in0(2'b00), .in1(Decoded_Instruction[11:10]), .out(multiplexer_2_out), .sel(comparator_5_eq));  // open: en
  Multiplexer #(.width(2)) multiplexer_3 (
    .in0(2'b00), .in1(Decoded_Instruction[11:10]), .out(multiplexer_3_out), .sel(comparator_5_eq));  // open: en
  Comparator #(.width(2), .mode("unsigned")) comparator_9 (
    .a(multiplexer_3_out), .b(2'b01), .eq(comparator_9_eq));  // open: gt, lt
  Comparator #(.width(2), .mode("unsigned")) comparator_10 (
    .a(multiplexer_2_out), .b(2'b11), .eq(comparator_10_eq));  // open: gt, lt
  or or_5 (or_5_out, comparator_6_eq, comparator_9_eq);
  or or_6 (or_6_out, or_5_out, comparator_10_eq);
  Clock clock_4 (.out(clock_4_out));
  and and_4 (Clock_R0, clock_4_out, or_5_out);
  and and_5 (Clock_R1, or_6_out, clock_5_out);
  Clock clock_5 (.out(clock_5_out));

  assign Select_Input_MUX_ULA = 1'b0;

  // Notes on the sheet:
  //   registers
  //   Opcode
  //   Estado setup - ponta pe inicial
  //   RD
  //   Sinal para habilitar a escrita no IR
  //   Sinal para habilitar a escrita no PC
  //   Sinal para habilitar a escrita no RA
  //   Sinal para habilitar a escrita na memória
  //   Envia o sinal com o OPCODE para a ULA
  //   Seleciona dentre RA  e PC a saída do mux, se 0 seleciona o RA se 1 seleciona o PC
  //   Seleciona dentre IR  e a  saída da ULA a saída do mux, se 0 seleciona o IR se 1 seleciona a saída da ULA
  //   Sinal para habilitar a escrita no R0
  //   Sinal para habilitar a escrita no R1
endmodule

module MType (
  input  [3:0] in_1,
  output Is_M_Type
);

  Comparator #(.width(4), .mode("unsigned")) comparator_1 (.a(in_1), .b(4'b0000), .eq(Is_M_Type));  // open: gt, lt
endmodule
